# Fritzing sketch memory-game (saved by Fritzing 0.9.10b)
breadboards: 1

parts:
  Part1 = Arduino Uno (Rev3) - ICSP
  S2 = Momentary Switch [package=ksa_sealed_tac_switch]
  S3 = Momentary Switch [package=ksa_sealed_tac_switch]
  S4 = Momentary Switch [package=ksa_sealed_tac_switch]
  LED1 = smd LED [color="Red (633nm)" package="1206 [SMD]"]
  LED2 = smd LED [color="Green (555nm)" package="1206 [SMD]"]
  LED3 = smd LED [color="Yellow (595nm)" package="1206 [SMD]"]
  LED4 = smd LED [color="Blue (505nm)" package="1206 [SMD]"]
  R1 = Resistor [tolerance=±5% resistance=330 package="0805 [SMD]"]
  R2 = Resistor [tolerance=±5% resistance=330 package="0805 [SMD]"]
  S1 = Momentary Switch [package=ksa_sealed_tac_switch]
  R3 = Resistor [tolerance=±5% resistance=330 package="0805 [SMD]"]
  R4 = Resistor [tolerance=±5% resistance=330 package="0805 [SMD]"]
  U2 = POT [knob_status=50% power=0.5W package=alps_pot]
  Grove1 = Grove OLED 128x96

nets:
  N1: Part1.A0, U2.S
  N2: Part1.ICSP_MOSI, Part1.D11_PWM/MOSI, S1.1
  N3: Part1.D8, S4.1
  N4: Part1.D9_PWM, S3.1
  N5: Part1.D10_PWM/SS, S2.1
  N6: Part1.A4/SDA, Grove1.SDA
  N7: Part1.A5/SCL, Grove1.SCL
  N8: Part1.D2, LED4.anode
  N9: Part1.D3_PWM, LED3.anode
  N10: Part1.D4, LED2.anode
  N11: Part1.D5_PWM, LED1.anode
  5V: Part1.5V, U2.A, Grove1.VCC
  GND: Part1.GND, S2.4, S3.4, S4.4, R1.Pin_0, R2.Pin_0, S1.4, R3.Pin_0, R4.Pin_0, U2.E, Grove1.GND
  N12: LED1.cathode, R1.Pin_1
  N13: LED2.cathode, R2.Pin_1
  N14: LED3.cathode, R3.Pin_1
  N15: LED4.cathode, R4.Pin_1
